# Fritzing sketch HC-SR04-Example (saved by Fritzing 0.9.1b)

parts:
  U1 = HC-SR04 [chip_label=IC package="SIP (Single Inline) [THT]"]
  Composant1 = Arduino Uno (Rev3)

nets:
  VCC: U1.Vcc, Composant1.5V
  N1: U1.Trig, Composant1.D4
  N2: U1.Echo, Composant1.D2
  GND: U1.GND, Composant1.GND

custom parts:
  HC-SR04: HC-SR04 ultrasound distance sensor
