# Fritzing sketch hc-05-serial (saved by Fritzing 0.9.1b)

parts:
  Part1 = Bluetooth HC-05 Macho
  Composant1 = Arduino Uno (Rev3)

nets:
  N1: Part1.TXD, Composant1.D7
  N2: Part1.RXD, Composant1.D8
  VCC: Part1.VCC, Composant1.5V
  GND: Part1.GND, Composant1.GND
