# Fritzing sketch motor_arduino (saved by Fritzing 0.9.1b)
breadboards: 1

parts:
  M1 = DC Motor
  VCC1 = Battery
  Composant1 = Arduino Uno (Rev3)
  IC1 = H-Bridge [package=THT]

nets:
  N1: M1.pin_1, IC1.3Y
  N2: M1.pin_2, IC1.4Y
  GND3: VCC1.-, IC1.GND3, IC1.GND4
  N3: VCC1.+, IC1.VCC1
  N4: Composant1.D8, IC1.3A
  N5: Composant1.D11_PWM/MOSI, IC1.3_4EN
  N6: Composant1.D3_PWM, IC1.4A
