# Fritzing sketch voiture_telecomande_4X4 (saved by Fritzing 0.9.1b)

parts:
  M1 = DC Motor
  IC1 = H-Bridge [package=THT]
  Composant1 = Arduino Uno (Rev3)
  VCC1 = Battery block 9V
  M2 = DC Motor
  Composant2 = Bluetooth Mate Silver
  IC2 = H-Bridge [package=THT]
  M3 = DC Motor
  M4 = DC Motor
  SPKR1 = Loudspeaker
  U2 = HC-SR04 [chip_label=IC package="SIP (Single Inline) [THT]"]

nets:
  N1: M1.pin_1, IC1.2Y
  N2: M1.pin_2, IC1.1Y
  N3: IC1.1_2EN, Composant1.D3_PWM, IC2.1_2EN
  N4: IC1.1A, Composant1.D12/MISO, IC2.1A
  GND: IC1.GND1, IC1.GND2, IC1.GND3, IC1.GND4, Composant1.GND, VCC1.+, Composant2.GND, IC2.GND1, IC2.GND2, IC2.GND3, IC2.GND4, SPKR1.pin2, U2.GND
  N5: IC1.2A, Composant1.D13/SCK, IC2.2A
  N6: IC1.VCC2, VCC1.-, IC2.VCC2
  N7: IC1.3_4EN, Composant1.D5_PWM, IC2.3_4EN
  N8: IC1.3A, Composant1.D10_PWM/SS, IC2.3A
  N9: IC1.3Y, M2.pin_1
  N10: IC1.4Y, M2.pin_2
  N11: IC1.4A, Composant1.D11_PWM/MOSI, IC2.4A
  VCC: IC1.VCC1, Composant1.5V, Composant2.VCC, U2.Vcc
  N12: Composant1.D8, Composant2.RX_5V
  N13: Composant1.D9_PWM, SPKR1.pin1
  N14: Composant1.D4, U2.Trig
  N15: Composant1.D6_PWM, U2.Echo
  N16: Composant1.D7, Composant2.TX_5V
  N17: IC2.1Y, M4.pin_1
  N18: IC2.2Y, M4.pin_2
  N19: IC2.3Y, M3.pin_2
  N20: IC2.4Y, M3.pin_1

custom parts:
  HC-SR04: HC-SR04 ultrasound distance sensor
